# Fritzing sketch schematic (saved by Fritzing 1.0.2b)
breadboards: 1

parts:
  AHT1 = AHT20 BMP280 pressure and humidity breakout
  Part1 = Arduino Uno (Rev3)

nets:
  VDD: AHT1.VDD, Part1.5V
  N1: AHT1.SDA, Part1.A4/SDA
  GND: AHT1.GND, Part1.GND
  N2: AHT1.SCL, Part1.A5/SCL

custom parts:
  AHT20 BMP280 pressure and humidity breakout: Cheap breakout board for the BMP280, barometric pressure sensor, and AHT20, humidity sensor
